// Digital circuit Sumador1bit.dig as structural Verilog
module Sumador1bit (
  input  A,
  input  B,
  input  Cin,
  output Y,
  output Cout
);

  wire and_1_out, and_2_out, xor_1_out;

  xor xor_1 (xor_1_out, A, B);
  and and_1 (and_1_out, A, B);
  and and_2 (and_2_out, xor_1_out, Cin);
  xor xor_2 (Y, xor_1_out, Cin);
  or or_1 (Cout, and_2_out, and_1_out);
endmodule
