// Digital circuit Sumador4bit.dig as structural Verilog
module Sumador4bit (
  input  A,
  input  B,
  input  Cin,
  input  C,
  input  D,
  input  E,
  input  F,
  input  G,
  input  H,
  output W,
  output X,
  output Y,
  output Z,
  output Cout
);

  wire and_1_out, and_2_out, and_3_out, and_4_out, and_5_out, and_6_out, and_7_out, and_8_out, or_1_out,
       or_2_out, or_3_out, xor_1_out, xor_3_out, xor_5_out, xor_7_out;

  xor xor_1 (xor_1_out, A, B);
  and and_1 (and_1_out, A, B);
  and and_2 (and_2_out, xor_1_out, Cin);
  xor xor_2 (W, xor_1_out, Cin);
  or or_1 (or_1_out, and_2_out, and_1_out);
  xor xor_3 (xor_3_out, C, D);
  and and_3 (and_3_out, C, D);
  and and_4 (and_4_out, xor_3_out, or_1_out);
  xor xor_4 (X, xor_3_out, or_1_out);
  or or_2 (or_2_out, and_4_out, and_3_out);
  xor xor_5 (xor_5_out, E, F);
  and and_5 (and_5_out, E, F);
  and and_6 (and_6_out, xor_5_out, or_2_out);
  xor xor_6 (Y, xor_5_out, or_2_out);
  or or_3 (or_3_out, and_6_out, and_5_out);
  xor xor_7 (xor_7_out, G, H);
  and and_7 (and_7_out, G, H);
  and and_8 (and_8_out, xor_7_out, or_3_out);
  xor xor_8 (Z, xor_7_out, or_3_out);
  or or_4 (Cout, and_8_out, and_7_out);

  // Notes on the sheet:
  //   MSB SALIDA
endmodule
