// Digital circuit reto1 .dig as structural Verilog
module reto1 (
  input  A0,
  input  A1,
  input  A2,
  input  A3,
  input  B0,
  input  B1,
  input  B2,
  input  B3,
  input  Cin_0,
  input  _0,
  output Burn,
  output Perfect,
  output Process
);

  wire and_1_out, and_2_out, and_3_out, and_4_out, and_5_out, and_6_out, and_7_out, and_8_out, or_1_out,
       or_2_out, or_3_out, or_4_out, xor_1_out, xor_2_out, xor_3_out, xor_4_out, xor_5_out, xor_6_out,
       xor_7_out, xor_8_out, xor_9_out, xor_10_out, xor_11_out, xor_12_out;

  xor xor_1 (xor_1_out, B0, Cin_0);
  xor xor_2 (xor_2_out, B1, Cin_0);
  xor xor_3 (xor_3_out, B2, Cin_0);
  xor xor_4 (xor_4_out, B3, Cin_0);
  xor xor_5 (xor_5_out, A0, xor_1_out);
  and and_1 (and_1_out, A0, xor_1_out);
  xor xor_6 (xor_6_out, A1, xor_2_out);
  and and_2 (and_2_out, A1, xor_2_out);
  xor xor_7 (xor_7_out, A2, xor_3_out);
  and and_3 (and_3_out, A2, xor_3_out);
  xor xor_8 (xor_8_out, A3, xor_4_out);
  and and_4 (and_4_out, A3, xor_4_out);
  and and_5 (and_5_out, xor_5_out, Cin_0);
  and and_6 (and_6_out, xor_6_out, or_1_out);
  and and_7 (and_7_out, xor_7_out, or_2_out);
  and and_8 (and_8_out, xor_8_out, or_3_out);
  xor xor_9 (xor_9_out, xor_6_out, or_1_out);
  xor xor_10 (xor_10_out, xor_5_out, Cin_0);
  or or_1 (or_1_out, and_5_out, and_1_out);
  or or_2 (or_2_out, and_6_out, and_2_out);
  xor xor_11 (xor_11_out, xor_7_out, or_2_out);
  or or_3 (or_3_out, and_7_out, and_3_out);
  xor xor_12 (xor_12_out, xor_8_out, or_3_out);
  or or_4 (or_4_out, and_8_out, and_4_out);
  Comp4ret comp4ret_1 (
    .A3(xor_12_out), .B3(_0), .A2(xor_11_out), .B2(_0), .A1(xor_9_out), .B1(_0), .A0(xor_10_out), .B0(_0),
    .Cout(or_4_out), .A_gt(Burn), .A_eq(Perfect), .A_lt(Process));
endmodule
